// Logisim project alu.circ as structural Verilog: 1 circuit, main circuit ALU
module ALU (
  input  [31:0] A,
  input  [31:0] B,
  input  [3:0] Op,
  output [31:0] Out
);

  wire comparator_1_lt, zero;
  wire [31:0] add, \and , div, mul, mulh, \or , rem, sll, slt, srl, sub, \xor ;

  Comparator #(.width(32)) comparator_1 (.a(A), .b(B), .lt(comparator_1_lt));  // open: gt, eq
  Subtractor #(.width(32)) subtractor_1 (.a(A), .b(B), .out(sub));  // open: bin, bout
  Shifter #(.width(32), .shift("ar")) shifter_1 (.in(A), .\dist ({5{1'b1}}), .out(srl));
  assign \and  = A & B;  // AND_Gate and_1, 32 bits wide
  assign \xor  = A ^ B;  // XOR_Gate xor_1, 32 bits wide
  Adder #(.width(32)) adder_1 (.a(A), .b(B), .out(add));  // open: cin, cout
  assign slt = {{31{1'b0}}, comparator_1_lt};  // Bit_Extender bit_extender_1
  assign \or  = A | B;  // OR_Gate or_1, 32 bits wide
  Multiplier #(.width(32)) multiplier_1 (.a(A), .b(B), .out(mulh));  // open: cin, cout
  Shifter #(.width(32)) shifter_2 (.in(A), .\dist ({5{1'b1}}), .out(sll));
  Divider #(.width(32)) divider_1 (.a(A), .b(B), .out(div));  // open: upper, rem
  Divider #(.width(32)) divider_2 (.a(A), .b(B), .out(rem));  // open: upper, rem
  Multiplier #(.width(32)) multiplier_2 (.a(A), .b(B), .out(mul));  // open: cin, cout
  Comparator #(.width(32)) comparator_2 (.a(Out), .b({32{1'b0}}), .eq(zero));  // open: gt, lt
  Multiplexer #(.select(4), .width(32), .enable("false")) multiplexer_1 (
    .in0(sll), .in1(srl), .in2(add), .in3(\and ), .in4(\or ), .in5(\xor ), .in6(slt), .in7(mul), .in8(mulh),
    .in9(div), .in10(rem), .in11(sub), .in12({32{1'b0}}), .in13({32{1'b0}}), .in14({32{1'b0}}),
    .in15({32{1'b0}}), .out(Out), .sel(Op));

  // Notes on the sheet:
  //   Inputs
  //   NOTE
  //   Please do not modify/replace/move/change/delete/etc input and output pins
  //   Outputs
endmodule
