// Logisim project cpu.circ as structural Verilog: 2 circuits, main circuit CPU
module CPU (
  input  [31:0] Instruction,
  input  CLK,
  output [31:0] s0,
  output [31:0] s1,
  output [31:0] t0,
  output [31:0] t1,
  output [31:0] a0,
  output [31:0] ra,
  output [31:0] sp,
  output [31:0] PC
);

  wire incrementer_1_p1;
  wire [31:0] immgen_1_s, multiplexer_1_out, regfile_1_r1, regfile_1_r2, wb;

  // Incrementer incrementer_1: pin names not known; wires that end beside it: incrementer_1_p1, PC
  // PC pc_1: pin names not known; wires that end beside it: incrementer_1_p1, CLK, PC
  RegFile regfile_1 (
    .clk(CLK), .r1(regfile_1_r1), .r2(regfile_1_r2), .we(1'b1), .w(wb), .rd(Instruction[11:7]),
    .rs1(Instruction[19:15]), .rs2(Instruction[24:20]));  // open: s0, s1, t0, t1, a0, ra, sp
  ImmGen immgen_1 (.E(Instruction), .S(immgen_1_s));  // open: in_2
  Multiplexer #(.width(32), .enable("false")) multiplexer_1 (
    .in0(regfile_1_r2), .in1(immgen_1_s), .out(multiplexer_1_out), .sel(1'b1));
  ALU alu_1 (.A(regfile_1_r1), .B(multiplexer_1_out), .Op(4'b0010), .Out(wb));
  // memory_main main_1: pin names not known

  // Other names for the same wires on the sheet: fetch_addr[31:0] = PC; INST[31:0] = Instruction

  // Notes on the sheet:
  //   NOTE
  //   Please do not modify/replace/move/change/delete/etc input and output pins
  //   These are debug/test outputs from your circuit
endmodule

module ImmGen (
  input  [31:0] E,
  input  in_2,
  output [31:0] S
);

  wire [11:0] undriven;
  wire [31:0] bit_extender_1_out;

  assign bit_extender_1_out = {{20{1'b0}}, undriven};  // Bit_Extender bit_extender_1
  Multiplexer #(.select(3), .width(32)) multiplexer_1 (
    .in0({32{1'b0}}), .in1(bit_extender_1_out), .out(S), .en(in_2));  // open: in2, in3, in4, in5, in6, in7, sel
endmodule
