// Logisim project proyecto info 3 prueba2.circ as structural Verilog: 1 circuit, main circuit main
module main (
  input  X
);

  wire A_q, and_1_out, and_2_out, and_3_out, and_4_out, B_q, C_q, clock_1_out, main_1_p5, main_1_p6,
       main_1_p7, main_1_p8, main_1_p9, main_1_p10, main_1_p11, main_1_p12, not_1_out, not_2_out, not_3_out,
       or_1_out, or_2_out, xor_1_out, xor_2_out, xor_3_out;

  Clock clock_1 (.out(clock_1_out));
  D_Flip_Flop C (.clk(clock_1_out), .D(or_2_out), .Q(C_q), .en(1'b1));  // open: Qn, preset, reset
  D_Flip_Flop B (.clk(clock_1_out), .D(or_1_out), .Q(B_q), .en(1'b1));  // open: Qn, preset, reset
  not not_1 (not_1_out, X);
  not not_2 (not_2_out, C_q);
  D_Flip_Flop A (.clk(clock_1_out), .D(xor_1_out), .Q(A_q), .en(1'b1));  // open: Qn, preset, reset
  not not_3 (not_3_out, X);
  xor xor_1 (xor_1_out, A_q, not_1_out);
  xor xor_2 (xor_2_out, A_q, B_q);
  and and_1 (and_1_out, not_2_out, X);
  and and_2 (and_2_out, not_3_out, xor_2_out);
  and and_3 (and_3_out, A_q, B_q);
  xor xor_3 (xor_3_out, and_3_out, C_q);
  or or_1 (or_1_out, and_1_out, and_2_out);
  // SevenSegment_main main_1: pin names not known; wires that end beside it: 1'b0, C_q, B_q, A_q, main_1_p5, main_1_p6, main_1_p7, main_1_p8, main_1_p9, main_1_p10, main_1_p11, main_1_p12
  and and_4 (and_4_out, X, B_q);
  _7_Segment_Display u_7_segment_display_1 (
    .g(main_1_p11), .f(main_1_p10), .a(main_1_p5), .b(main_1_p6), .e(main_1_p9), .d(main_1_p8),
    .c(main_1_p7), .dp(main_1_p12));
  or or_2 (or_2_out, xor_3_out, and_4_out);
endmodule
