// Logisim project regfile.circ as structural Verilog: 1 circuit, main circuit RegFile
module RegFile (
  input  [4:0] rd,
  input  [4:0] rs1,
  input  [4:0] rs2,
  input  [31:0] w,
  input  we,
  input  clk,
  output [31:0] s0,
  output [31:0] s1,
  output [31:0] t0,
  output [31:0] t1,
  output [31:0] a0,
  output [31:0] ra,
  output [31:0] sp,
  output [31:0] r1,
  output [31:0] r2
);

  wire and_1_out, and_2_out, and_3_out, and_4_out, and_5_out, and_6_out, and_7_out, decoder_1_out1,
       decoder_1_out2, decoder_1_out5, decoder_1_out6, decoder_1_out8, decoder_1_out9, decoder_1_out10;

  Decoder #(.select(5), .enable("false")) decoder_1 (
    .out1(decoder_1_out1), .out2(decoder_1_out2), .out5(decoder_1_out5), .out6(decoder_1_out6),
    .out8(decoder_1_out8), .out9(decoder_1_out9), .out10(decoder_1_out10), .sel(rd));  // open: out0, out3, out4, out7, out11, out12, out13, out14, out15, out16, out17, out18, out19, out20, out21, out22, out23, out24, out25, out26, out27, out28, out29, out30, out31
  and and_1 (and_1_out, decoder_1_out1, we);
  and and_2 (and_2_out, decoder_1_out2, we);
  and and_3 (and_3_out, decoder_1_out5, we);
  and and_4 (and_4_out, decoder_1_out6, we);
  and and_5 (and_5_out, decoder_1_out8, we);
  and and_6 (and_6_out, decoder_1_out9, we);
  and and_7 (and_7_out, decoder_1_out10, we);
  Register #(.width(32)) register_1 (.D(w), .en(and_1_out), .Q(ra), .clk(clk));  // open: clr
  Register #(.width(32)) register_2 (.D(w), .en(and_2_out), .Q(sp), .clk(clk));  // open: clr
  Register #(.width(32)) register_3 (.D(w), .en(and_3_out), .Q(t0), .clk(clk));  // open: clr
  Register #(.width(32)) register_4 (.D(w), .en(and_4_out), .Q(t1), .clk(clk));  // open: clr
  Register #(.width(32)) register_5 (.D(w), .en(and_5_out), .Q(s0), .clk(clk));  // open: clr
  Register #(.width(32)) register_6 (.D(w), .en(and_6_out), .Q(s1), .clk(clk));  // open: clr
  Register #(.width(32)) register_7 (.D(w), .en(and_7_out), .Q(a0), .clk(clk));  // open: clr
  Multiplexer #(.select(5), .width(32), .enable("false")) multiplexer_1 (
    .in0({32{1'b0}}), .in1(ra), .in2(sp), .in3({32{1'b0}}), .in4({32{1'b0}}), .in5(t0), .in6(t1),
    .in7({32{1'b0}}), .in8(s0), .in9(s1), .in10(a0), .in11({32{1'b0}}), .in12({32{1'b0}}), .in13({32{1'b0}}),
    .in14({32{1'b0}}), .in15({32{1'b0}}), .in16({32{1'b0}}), .in17({32{1'b0}}), .in18({32{1'b0}}),
    .in19({32{1'b0}}), .in20({32{1'b0}}), .in21({32{1'b0}}), .in22({32{1'b0}}), .in23({32{1'b0}}),
    .in24({32{1'b0}}), .in25({32{1'b0}}), .in26({32{1'b0}}), .in27({32{1'b0}}), .in28({32{1'b0}}),
    .in29({32{1'b0}}), .in30({32{1'b0}}), .in31({32{1'b0}}), .out(r1), .sel(rs1));
  Multiplexer #(.select(5), .width(32), .enable("false")) multiplexer_2 (
    .in0({32{1'b0}}), .in1(ra), .in2(sp), .in3({32{1'b0}}), .in4({32{1'b0}}), .in5(t0), .in6(t1),
    .in7({32{1'b0}}), .in8(s0), .in9(s1), .in10(a0), .in11({32{1'b0}}), .in12({32{1'b0}}), .in13({32{1'b0}}),
    .in14({32{1'b0}}), .in15({32{1'b0}}), .in16({32{1'b0}}), .in17({32{1'b0}}), .in18({32{1'b0}}),
    .in19({32{1'b0}}), .in20({32{1'b0}}), .in21({32{1'b0}}), .in22({32{1'b0}}), .in23({32{1'b0}}),
    .in24({32{1'b0}}), .in25({32{1'b0}}), .in26({32{1'b0}}), .in27({32{1'b0}}), .in28({32{1'b0}}),
    .in29({32{1'b0}}), .in30({32{1'b0}}), .in31({32{1'b0}}), .out(r2), .sel(rs2));

  // Notes on the sheet:
  //   Write Register
  //   Read Register 1
  //   Read Register 2
  //   Write Data
  //   Write Enable
  //   Clock
  //   NOTE
  //   Please do not modify/replace/move/change/delete/etc input and output pins
  //   These are debug/test outputs from your circuit
  //   Read Data 1
  //   Read Data 2
endmodule
